# Fritzing sketch PROJ002 (saved by Fritzing 0.9.3b)
breadboards: 1

parts:
  Componente1 = Arduino Nano (Rev3.0)
  Cama_esquerra = Basic Servo
  Peu_dret = Basic Servo
  Peu_esquerre = Basic Servo
  Cama_dreta = Basic Servo
  BT1 = Bluetooth HC-06u [package=THT]
  2x18650_bat_(7_4Vcc) = 4 x AAA Battery Mount
  S1 = Round Pushbutton

nets:
  GND: Componente1.GND, Cama_esquerra.gnd, Peu_dret.gnd, Peu_esquerre.gnd, Cama_dreta.gnd, BT1.GND, 2x18650_bat_(7_4Vcc).-
  N1: Componente1.D2, BT1.RXD
  N2: Componente1.D4, BT1.TXD
  N3: Componente1.D7, Cama_dreta.pulse
  N4: Componente1.D8, Peu_esquerre.pulse
  N5: Componente1.D9, Peu_dret.pulse
  N6: Componente1.D10, Cama_esquerra.pulse
  VCC: Componente1.VIN, Cama_esquerra.vcc, Peu_dret.vcc, Peu_esquerre.vcc, Cama_dreta.vcc, S1.leg1
  5V: Componente1.5V, BT1.VCC
  N7: 2x18650_bat_(7_4Vcc).+, S1.leg0

custom parts:
  Bluetooth HC-06u: Bluetooth HC-06 - face up, pins down 16.5mm x 37.5mm PCB
